// Logisim project ALU.circ as structural Verilog
module AU (
  input  [7:0] A1,
  input  [7:0] A2,
  input  C1,
  output [7:0] out_4
);

  wire [7:0] adder_1_out, multiplexer_1_out, not_1_out;

  Adder adder_1 (.a(8'h1), .b(not_1_out), .out(adder_1_out));  // open: cin, cout
  assign not_1_out = ~A1;  // NOT_Gate not_1, 8 bits wide
  Multiplexer #(.enable("false"), .width(8)) multiplexer_1 (
    .in0(adder_1_out), .in1(A1), .out(multiplexer_1_out), .sel(C1));
  Adder adder_2 (.a(multiplexer_1_out), .b(A2), .out(out_4));  // open: cin, cout

  // Notes on the sheet:
  //   0-     1+
endmodule

module LU (
  input  [7:0] B1,
  input  [7:0] B2,
  input  C2,
  output [7:0] out_4
);

  wire [7:0] and_1_out, or_1_out;

  assign or_1_out = B1 | B2;  // OR_Gate or_1, 8 bits wide
  assign and_1_out = B1 & B2;  // AND_Gate and_1, 8 bits wide
  Multiplexer #(.enable("false"), .width(8)) multiplexer_1 (.in0(or_1_out), .in1(and_1_out), .out(out_4), .sel(C2));

  // Notes on the sheet:
  //   0 or 1 and
endmodule

module ALU (
  input  [7:0] A,
  input  [7:0] B,
  input  [3:0] Control,
  output [7:0] ALUOUT
);

  wire [7:0] au_1_out_4, lu_1_out_4;

  LU lu_1 (.B1(B), .B2(A), .C2(Control[3]), .out_4(lu_1_out_4));
  AU au_1 (.A1(B), .A2(A), .C1(Control[1]), .out_4(au_1_out_4));
  Multiplexer #(.enable("false"), .width(8)) multiplexer_1 (
    .in0(lu_1_out_4), .in1(au_1_out_4), .out(ALUOUT), .sel(Control[2]));

  // Notes on the sheet:
  //   x000 lu or
  //   x001 lu and
  //   x100 au -
  //   x110 au +
endmodule

module RegisterGroup (
  input  [4:0] ReadAddress,
  input  [7:0] Data,
  input  [4:0] WriteAddress,
  input  WE,
  input  Clock,
  output [7:0] RegisterOut
);

  wire and_1_out, and_2_out, and_3_out, and_4_out, and_5_out, and_6_out, and_7_out, and_8_out,
       decoder_1_out0, decoder_1_out1, decoder_1_out2, decoder_1_out3, decoder_1_out4, decoder_1_out5,
       decoder_1_out7;
  wire [7:0] register_1_q, register_2_q, register_3_q, register_4_q, register_5_q, register_6_q,
       register_7_q, register_8_q;

  Decoder #(.select(3)) decoder_1 (
    .out0(decoder_1_out0), .out1(decoder_1_out1), .out2(decoder_1_out2), .out3(decoder_1_out3),
    .out4(decoder_1_out4), .out5(decoder_1_out5), .out6(decoder_1_out5), .out7(decoder_1_out7),
    .sel(WriteAddress[2:0]));  // open: en
  and and_1 (and_1_out, decoder_1_out0, WE);
  and and_2 (and_2_out, decoder_1_out1, WE);
  and and_3 (and_3_out, decoder_1_out2, WE);
  and and_4 (and_4_out, decoder_1_out3, WE);
  and and_5 (and_5_out, decoder_1_out4, WE);
  and and_6 (and_6_out, decoder_1_out5, WE);
  and and_7 (and_7_out, decoder_1_out5, WE);
  and and_8 (and_8_out, decoder_1_out7, WE);
  Register register_1 (.D(Data), .en(and_1_out), .clk(Clock), .Q(register_1_q));  // open: clr
  Register register_2 (.D(Data), .en(and_2_out), .clk(Clock), .Q(register_2_q));  // open: clr
  Register register_3 (.D(Data), .en(and_3_out), .clk(Clock), .Q(register_3_q));  // open: clr
  Register register_4 (.D(Data), .en(and_4_out), .clk(Clock), .Q(register_4_q));  // open: clr
  Register register_5 (.D(Data), .en(and_5_out), .clk(Clock), .Q(register_5_q));  // open: clr
  Register register_6 (.D(Data), .en(and_6_out), .clk(Clock), .Q(register_6_q));  // open: clr
  Register register_7 (.D(Data), .en(and_7_out), .clk(Clock), .Q(register_7_q));  // open: clr
  Register register_8 (.D(Data), .en(and_8_out), .clk(Clock), .Q(register_8_q));  // open: clr
  Multiplexer #(.enable("false"), .select(3), .width(8)) multiplexer_1 (
    .in0(register_1_q), .in1(register_2_q), .in2(register_3_q), .in3(register_4_q), .in4(register_5_q),
    .in5(register_6_q), .in6(register_7_q), .in7(register_8_q), .out(RegisterOut), .sel(ReadAddress[2:0]));
endmodule

module CPU (
);

  wire clock_1_out, clock_2_out, clock_3_out, not_1_out;
  wire [3:0] bit_extender_3_out;
  wire [4:0] rom_1_data_3, rom_1_data_4;
  wire [5:0] rom_1_data;
  wire [7:0] alu_1_aluout, bit_extender_1_out, bit_extender_2_out, multiplexer_1_out, pc_1_pcout, ram_1_dout,
       registergroupforram_1_rout0, registergroupforram_1_rout1;
  wire [9:0] rom_1_data_2;
  wire [31:26] rom_1_data_5;

  ROM #(.dataWidth(32)) rom_1 (
    .addr(pc_1_pcout), .data({rom_1_data_5, rom_1_data_4, rom_1_data_3, rom_1_data_2, rom_1_data}));
  Bit_Extender #(.in_width(32), .out_width(8)) bit_extender_1 (
    .in({rom_1_data_5, rom_1_data_4, rom_1_data_3, rom_1_data_2, rom_1_data}), .out(bit_extender_1_out));
  Clock clock_1 (.out(clock_1_out));
  PC pc_1 (.jmp(rom_1_data_5[28]), .pos(bit_extender_1_out), .CLK(clock_1_out), .PCout(pc_1_pcout));
  Bit_Extender #(.in_width(10), .out_width(8)) bit_extender_2 (.in(rom_1_data_2), .out(bit_extender_2_out));
  Bit_Extender #(.in_width(6), .out_width(4)) bit_extender_3 (.in(rom_1_data), .out(bit_extender_3_out));
  Clock clock_2 (.out(clock_2_out));
  Multiplexer #(.enable("false"), .width(8)) multiplexer_1 (
    .in0(alu_1_aluout), .in1(ram_1_dout), .out(multiplexer_1_out), .sel(rom_1_data_5[30]));
  RegisterGroupForRAM registergroupforram_1 (
    .Data(multiplexer_1_out), .Read0(rom_1_data_4), .Read1(rom_1_data_3), .WriteAddress(rom_1_data_3),
    .WE(rom_1_data_5[31]), .Clock(clock_2_out), .Rout0(registergroupforram_1_rout0),
    .Rout1(registergroupforram_1_rout1));
  ALU alu_1 (
    .A(registergroupforram_1_rout0), .B(bit_extender_2_out), .Control(bit_extender_3_out),
    .ALUOUT(alu_1_aluout));
  Clock clock_3 (.out(clock_3_out));
  RAM ram_1 (
    .addr(alu_1_aluout), .we(rom_1_data_5[29]), .oe(not_1_out), .clk(clock_3_out),
    .din(registergroupforram_1_rout1), .dout(ram_1_dout));
  not not_1 (not_1_out, rom_1_data_5[29]);

  // Notes on the sheet:
  //   contents of rom_1 (hex, n*v repeats v):
  //   84e00046 84e10106 24010006 c4010006 84210046 24010006 10000003
endmodule

module RegisterGroupForRAM (
  input  [7:0] Data,
  input  [4:0] Read0,
  input  [4:0] Read1,
  input  [4:0] WriteAddress,
  input  WE,
  input  Clock,
  output [7:0] Rout0,
  output [7:0] Rout1
);

  wire and_1_out, and_2_out, and_3_out, and_4_out, and_5_out, and_6_out, and_7_out, decoder_1_out0,
       decoder_1_out1, decoder_1_out2, decoder_1_out3, decoder_1_out4, decoder_1_out5, decoder_1_out7;
  wire [2:0] bit_extender_1_out, bit_extender_2_out, bit_extender_3_out;
  wire [7:0] register_1_q, register_2_q, register_3_q, register_4_q, register_5_q, register_6_q,
       register_7_q, register_8_q;

  Bit_Extender #(.in_width(5), .out_width(3)) bit_extender_1 (.in(Read0), .out(bit_extender_1_out));
  Bit_Extender #(.in_width(5), .out_width(3)) bit_extender_2 (.in(Read1), .out(bit_extender_2_out));
  Bit_Extender #(.in_width(5), .out_width(3)) bit_extender_3 (.in(WriteAddress), .out(bit_extender_3_out));
  Decoder #(.select(3)) decoder_1 (
    .out0(decoder_1_out0), .out1(decoder_1_out1), .out2(decoder_1_out2), .out3(decoder_1_out3),
    .out4(decoder_1_out4), .out5(decoder_1_out5), .out6(decoder_1_out5), .out7(decoder_1_out7),
    .sel(bit_extender_3_out));  // open: en
  and and_1 (and_1_out, decoder_1_out0, WE);
  and and_2 (and_2_out, decoder_1_out1, WE);
  and and_3 (and_3_out, decoder_1_out2, WE);
  and and_4 (and_4_out, decoder_1_out3, WE);
  and and_5 (and_5_out, decoder_1_out4, WE);
  and and_6 (and_6_out, decoder_1_out5, WE);
  and and_7 (and_7_out, decoder_1_out5, WE);
  // AND_Gate and_8 has open pins: in0=decoder_1_out7, in1=WE, out=open
  Register register_1 (.D(Data), .en(and_1_out), .clk(Clock), .Q(register_1_q));  // open: clr
  Register register_2 (.D(Data), .en(and_2_out), .clk(Clock), .Q(register_2_q));  // open: clr
  Register register_3 (.D(Data), .en(and_3_out), .clk(Clock), .Q(register_3_q));  // open: clr
  Register register_4 (.D(Data), .en(and_4_out), .clk(Clock), .Q(register_4_q));  // open: clr
  Register register_5 (.D(Data), .en(and_5_out), .clk(Clock), .Q(register_5_q));  // open: clr
  Register register_6 (.D(Data), .en(and_6_out), .clk(Clock), .Q(register_6_q));  // open: clr
  Register register_7 (.D(Data), .en(and_7_out), .clk(Clock), .Q(register_7_q));  // open: clr
  Register register_8 (.Q(register_8_q), .clr(1'b1));  // open: D, en, clk
  Multiplexer #(.enable("false"), .select(3), .width(8)) multiplexer_1 (
    .in0(register_1_q), .in1(register_2_q), .in2(register_3_q), .in3(register_4_q), .in4(register_5_q),
    .in5(register_6_q), .in6(register_7_q), .in7(register_8_q), .out(Rout0), .sel(bit_extender_1_out));
  Multiplexer #(.enable("false"), .select(3), .width(8)) multiplexer_2 (
    .in0(register_1_q), .in1(register_2_q), .in2(register_3_q), .in3(register_4_q), .in4(register_5_q),
    .in5(register_6_q), .in6(register_7_q), .in7(register_8_q), .out(Rout1), .sel(bit_extender_2_out));
endmodule

module PC (
  input  jmp,
  input  [7:0] pos,
  input  CLK,
  output [7:0] PCout
);

  wire [7:0] adder_1_out, multiplexer_1_out;

  Multiplexer #(.enable("false"), .width(8)) multiplexer_1 (
    .in0(adder_1_out), .in1(pos), .out(multiplexer_1_out), .sel(jmp));
  Register register_1 (.D(multiplexer_1_out), .en(1'b1), .clk(CLK), .Q(PCout));  // open: clr
  Adder adder_1 (.a(PCout), .b(8'h1), .out(adder_1_out));  // open: cin, cout
endmodule
